# Fritzing sketch circuit (saved by Fritzing 0.9.0b)
breadboards: 1

parts:
  Part1 = Arduino Uno (Rev3)
  J1 = Basic Servo
  M1 = Stepper Motor - Bipolar  # not connected
  J2 = Piezo Speaker
  LED1 = LED - 5mm [color="Red (633nm)" package="5 mm [THT]"]
  R1 = Resistor [tolerance=±5% resistance=220 package=THT]

nets:
  N1: Part1.D9_PWM, J1.pulse
  N2: Part1.D10_PWM/SS, R1.Pin_1
  N3: Part1.D12/MISO, J2.pin2
  GND: Part1.GND, J1.gnd, J2.pin1, LED1.cathode
  5V: Part1.5V, J1.vcc
  N4: LED1.anode, R1.Pin_0
